// Logisim project 12363006_4.circ as structural Verilog: 5 circuits, main circuit ALU
module HalfAdder (
  input  in_1,
  input  in_2,
  output out_3,
  output out_4
);

  and and_1 (out_3, in_1, in_2);
  or or_1 (out_4, in_1, in_2);
endmodule

module _1BitFullAdder (
  input  X,
  input  Y,
  input  CarryIn,
  output CarryOut,
  output Sum
);

  wire and_1_out, and_2_out, xor_1_out;

  and and_1 (and_1_out, X, Y);
  and and_2 (and_2_out, xor_1_out, CarryIn);
  xor xor_1 (xor_1_out, X, Y);
  xor xor_2 (Sum, xor_1_out, CarryIn);
  or or_1 (CarryOut, and_1_out, and_2_out);
endmodule

module _4BitFullAdder (
  input  [3:0] Input1,
  input  [3:0] Input2,
  input  CarryIn,
  output CarryOut,
  output [3:0] Sum
);

  wire n1bitfulladder_2_carryout, n1bitfulladder_3_carryout, n1bitfulladder_4_carryout;

  _1BitFullAdder u_1bitfulladder_1 (
    .X(Input1[3]), .Y(Input2[3]), .CarryIn(n1bitfulladder_2_carryout), .CarryOut(CarryOut), .Sum(Sum[3]));
  _1BitFullAdder u_1bitfulladder_2 (
    .X(Input1[2]), .Y(Input2[2]), .CarryIn(n1bitfulladder_3_carryout), .CarryOut(n1bitfulladder_2_carryout),
    .Sum(Sum[2]));
  _1BitFullAdder u_1bitfulladder_3 (
    .X(Input1[1]), .Y(Input2[1]), .CarryIn(n1bitfulladder_4_carryout), .CarryOut(n1bitfulladder_3_carryout),
    .Sum(Sum[1]));
  _1BitFullAdder u_1bitfulladder_4 (
    .X(Input1[0]), .Y(Input2[0]), .CarryIn(CarryIn), .CarryOut(n1bitfulladder_4_carryout), .Sum(Sum[0]));
endmodule

module ALU (
  input  [3:0] Input1,
  input  [3:0] Input2,
  input  [1:0] ControlBits,
  output CarryOut,
  output [3:0] Output,
  output Zero
);

  wire [3:0] and_1_out, and_2_out, and_3_out, Combined_Adder_out_5, not_1_out;

  CombinedAdder Combined_Adder (
    .Input1(Input1), .Input2(Input2), ._0_for_addition_____1_for_subtract(ControlBits[1]),
    .CarryOut(CarryOut), .out_5(Combined_Adder_out_5));
  assign and_1_out = Input1 & Input2;  // AND_Gate and_1, 4 bits wide
  assign and_2_out = Combined_Adder_out_5 & not_1_out;  // AND_Gate and_2, 4 bits wide
  assign not_1_out = ~{4{ControlBits[0]}};  // NOT_Gate not_1, 4 bits wide
  assign and_3_out = and_1_out & {4{ControlBits[0]}};  // AND_Gate and_3, 4 bits wide
  assign Output = and_2_out | and_3_out;  // OR_Gate or_1, 4 bits wide
  nor nor_1 (Zero, Output[0], Output[1], Output[2], Output[3]);

  // Notes on the sheet:
  //   First control bit:
  //   1 = Subtraction
  //   0 = Addition
  //   Second control bit set to 1 for AND
endmodule

module CombinedAdder (
  input  [3:0] Input1,
  input  [3:0] Input2,
  input  _0_for_addition_____1_for_subtract,
  output CarryOut,
  output [3:0] out_5
);

  wire and_1_out, and_2_out, n4bitfulladder_1_carryout, n4bitfulladder_2_carryout, not_2_out;
  wire [3:0] and_3_out, and_4_out, n4bitfulladder_1_sum, n4bitfulladder_2_sum, not_1_out, not_3_out;

  assign not_1_out = ~Input2;  // NOT_Gate not_1, 4 bits wide
  _4BitFullAdder u_4bitfulladder_1 (
    .Input1(Input1), .Input2(Input2), .CarryIn(1'b0), .CarryOut(n4bitfulladder_1_carryout),
    .Sum(n4bitfulladder_1_sum));
  _4BitFullAdder u_4bitfulladder_2 (
    .Input1(Input1), .Input2(not_1_out), .CarryIn(1'b1), .CarryOut(n4bitfulladder_2_carryout),
    .Sum(n4bitfulladder_2_sum));
  and and_1 (and_1_out, n4bitfulladder_1_carryout, not_2_out);
  not not_2 (not_2_out, _0_for_addition_____1_for_subtract);
  and and_2 (and_2_out, n4bitfulladder_2_carryout, _0_for_addition_____1_for_subtract);
  assign and_3_out = n4bitfulladder_1_sum & not_3_out;  // AND_Gate and_3, 4 bits wide
  assign not_3_out = ~{4{_0_for_addition_____1_for_subtract}};  // NOT_Gate not_3, 4 bits wide
  assign and_4_out = n4bitfulladder_2_sum & {4{_0_for_addition_____1_for_subtract}};  // AND_Gate and_4, 4 bits wide
  or or_1 (CarryOut, and_1_out, and_2_out);
  assign out_5 = and_3_out | and_4_out;  // OR_Gate or_2, 4 bits wide
endmodule
