// Logisim project Q4B1.circ as structural Verilog: 1 circuit, main circuit main
module main (
  input  Reset,
  output MSB,
  output out_3,
  output out_4,
  output out_5,
  output out_6,
  output out_7,
  output out_8,
  output LSB
);

  wire clock_1_out;
  wire [7:0] adder_1_out, and_1_out;

  assign and_1_out = adder_1_out & {8{Reset}};  // AND_Gate and_1, 8 bits wide
  Register register_1 (
    .D(and_1_out), .Q({MSB, out_3, out_4, out_5, out_6, out_7, out_8, LSB}), .clk(clock_1_out));  // open: en, clr
  Clock clock_1 (.out(clock_1_out));
  Adder adder_1 (
    .a({MSB, out_3, out_4, out_5, out_6, out_7, out_8, LSB}), .b(8'h1), .out(adder_1_out));  // open: cin, cout

  // Notes on the sheet:
  //   Clock
endmodule
