// Logisim project Q4B2.circ as structural Verilog: 1 circuit, main circuit main
module main (
  input  [7:0] in_1,
  input  [7:0] in_2,
  input  Reset,
  input  Mem_Read_Write,
  output out_5,
  output out_6,
  output out_7,
  output out_8,
  output out_9,
  output out_10,
  output out_11,
  output out_12
);

  wire clock_1_out, not_1_out;

  assign {out_5, out_6, out_7, out_8, out_9, out_10, out_11, out_12} = Mem_Read_Write ? in_1 : 8'bz;  // Controlled_Buffer controlled_buffer_1
  Clock clock_1 (.out(clock_1_out));
  not not_1 (not_1_out, Mem_Read_Write);
  RAM ram_1 (
    .addr(in_2), .data({out_5, out_6, out_7, out_8, out_9, out_10, out_11, out_12}), .sel(1'b1),
    .clk(clock_1_out), .ld(not_1_out), .clr(Reset));

  // Notes on the sheet:
  //   Data In
  //   Address
  //   Clock
  //   Data Out
endmodule
