// Logisim project Diarmuid_Ryan_11363776_A4.circ as structural Verilog: 7 circuits, main circuit main
module main (
  input  CLK,
  input  [3:0] RegOut1,
  input  [3:0] RegOut2,
  input  [1:0] RegRead1,
  input  [1:0] RegRead2,
  input  [3:0] WriteData,
  input  [1:0] RegWrite,
  input  RegWrite_2,
  input  [3:0] MemAdd,
  input  ExtDataWrite,
  input  MemWrite,
  input  [3:0] ExtData,
  output [3:0] DataOut
);

  c c_1 (
    .ReadReg1(RegRead1), .MemAddress(MemAdd), .WriteReg(RegWrite), .RegWite(RegWrite_2), .ReadReg2(RegRead2),
    .MemWrite(MemWrite), .CLK(CLK), .MemDataOut(DataOut), .ExtMemWrite(ExtDataWrite), .ExtMemData(ExtData),
    .RegRead1(RegOut2), .RegRead1_2(RegOut1), .WriteData(WriteData));
  DotMatrix #(.matrixcols(4), .matrixrows(1)) dotmatrix_1 (
    .col0(DataOut[3]), .col1(DataOut[2]), .col2(DataOut[1]), .col3(DataOut[0]));
endmodule

module reg_file (
  input  [3:0] WriteData,
  input  [1:0] WriteReg,
  input  [1:0] ReadReg1,
  input  [1:0] ReadReg2,
  input  RegWrite,
  input  Clock,
  output [3:0] ReadData1,
  output [3:0] ReadData2
);

  wire and_1_out, and_2_out, and_3_out, and_4_out, decoder_1_out0, decoder_1_out1, decoder_1_out2,
       decoder_1_out3;
  wire [3:0] multiplexer_1_out, multiplexer_2_out, multiplexer_3_out, multiplexer_4_out, register_1_q,
       register_2_q, register_3_q, register_4_q;

  Decoder #(.select(2), .enable("false")) decoder_1 (
    .out0(decoder_1_out0), .out1(decoder_1_out1), .out2(decoder_1_out2), .out3(decoder_1_out3), .sel(WriteReg));
  and and_1 (and_1_out, decoder_1_out0, RegWrite);
  and and_2 (and_2_out, decoder_1_out1, RegWrite);
  and and_3 (and_3_out, decoder_1_out2, RegWrite);
  and and_4 (and_4_out, decoder_1_out3, RegWrite);
  Multiplexer #(.width(4), .enable("false")) multiplexer_1 (
    .in0(register_1_q), .in1(WriteData), .out(multiplexer_1_out), .sel(and_1_out));
  Multiplexer #(.width(4), .enable("false")) multiplexer_2 (
    .in0(register_2_q), .in1(WriteData), .out(multiplexer_2_out), .sel(and_2_out));
  Multiplexer #(.width(4), .enable("false")) multiplexer_3 (
    .in0(register_3_q), .in1(WriteData), .out(multiplexer_3_out), .sel(and_3_out));
  Multiplexer #(.width(4), .enable("false")) multiplexer_4 (
    .in0(register_4_q), .in1(WriteData), .out(multiplexer_4_out), .sel(and_4_out));
  Register #(.width(4)) register_1 (.D(multiplexer_1_out), .Q(register_1_q), .clk(Clock));  // open: en, clr
  Register #(.width(4)) register_2 (.D(multiplexer_2_out), .Q(register_2_q), .clk(Clock));  // open: en, clr
  Register #(.width(4)) register_3 (.D(multiplexer_3_out), .Q(register_3_q), .clk(Clock));  // open: en, clr
  Register #(.width(4)) register_4 (.D(multiplexer_4_out), .Q(register_4_q), .clk(Clock));  // open: en, clr
  Multiplexer #(.select(2), .width(4), .enable("false")) multiplexer_5 (
    .in0(register_1_q), .in1(register_2_q), .in2(register_3_q), .in3(register_4_q), .out(ReadData1),
    .sel(ReadReg1));
  Multiplexer #(.select(2), .width(4), .enable("false")) multiplexer_6 (
    .in0(register_1_q), .in1(register_2_q), .in2(register_3_q), .in3(register_4_q), .out(ReadData2),
    .sel(ReadReg2));

  // Notes on the sheet:
  //   Register File 4x4-bits
endmodule

module a (
  input  [3:0] A,
  input  [3:0] DataLoad,
  input  CLK,
  input  Store,
  output [3:0] DataOut
);

  wire not_1_out;

  not not_1 (not_1_out, Store);
  RAM #(.addrWidth(4), .dataWidth(4), .bus("separate")) ram_1 (
    .addr(A), .din(DataLoad), .data(DataOut), .str(Store), .clk(CLK), .ld(not_1_out));  // open: sel, clr
  DotMatrix #(.matrixcols(4), .matrixrows(1)) dotmatrix_1 (
    .col0(DataOut[3]), .col1(DataOut[2]), .col2(DataOut[1]), .col3(DataOut[0]));
endmodule

module b (
  input  [3:0] Address,
  input  [3:0] Offset,
  input  [3:0] DataLoad,
  input  Store,
  input  CLK,
  output [3:0] DataOut
);

  wire [3:0] adder_1_out;

  Adder #(.width(4)) adder_1 (.a(Address), .b(Offset), .out(adder_1_out));  // open: cin, cout
  a a_1 (.A(adder_1_out), .DataLoad(DataLoad), .Store(Store), .DataOut(DataOut), .CLK(CLK));
  DotMatrix #(.matrixcols(4), .matrixrows(1)) dotmatrix_1 (
    .col0(DataOut[3]), .col1(DataOut[2]), .col2(DataOut[1]), .col3(DataOut[0]));
endmodule

module c (
  input  [1:0] ReadReg1,
  input  [3:0] MemAddress,
  input  [3:0] WriteData,
  input  [1:0] WriteReg,
  input  RegWite,
  input  [1:0] ReadReg2,
  input  MemWrite,
  input  [3:0] ExtMemData,
  input  ExtMemWrite,
  input  CLK,
  output [3:0] RegRead1,
  output [3:0] RegRead1_2,
  output [3:0] MemDataOut
);

  wire [3:0] writeselector_1_data;

  reg_file reg_file_1 (
    .WriteData(WriteData), .WriteReg(WriteReg), .RegWrite(RegWite), .Clock(CLK), .ReadData1(RegRead1),
    .ReadReg1(ReadReg1), .ReadData2(RegRead1_2), .ReadReg2(ReadReg2));
  WriteSelector writeselector_1 (
    .ExtWrite(ExtMemWrite), .IntData(RegRead1_2), .ExtData(ExtMemData), .Data(writeselector_1_data));
  b b_1 (
    .Address(MemAddress), .Offset(RegRead1), .DataLoad(writeselector_1_data), .Store(MemWrite),
    .DataOut(MemDataOut), .CLK(CLK));
endmodule

module WriteSelector (
  input  ExtWrite,
  input  [3:0] IntData,
  input  [3:0] ExtData,
  output [3:0] Data
);

  wire [3:0] and_1_out, and_2_out, not_1_out;

  assign not_1_out = ~{4{ExtWrite}};  // NOT_Gate not_1, 4 bits wide
  assign and_1_out = not_1_out & IntData;  // AND_Gate and_1, 4 bits wide
  assign and_2_out = {4{ExtWrite}} & ExtData;  // AND_Gate and_2, 4 bits wide
  assign Data = and_1_out | and_2_out;  // OR_Gate or_1, 4 bits wide
endmodule

module _4C_3 (
  input  [1:0] ReadReg1,
  input  [3:0] MemAddress,
  input  [1:0] WriteReg,
  input  RegWite,
  input  [1:0] ReadReg2,
  input  MemWrite,
  input  [3:0] ExtMemData,
  input  ExtMemWrite,
  input  CLK,
  output [3:0] MemDataOut
);

  wire [3:0] reg_file_1_readdata1, reg_file_1_readdata2, writeselector_1_data;

  reg_file reg_file_1 (
    .WriteData(MemDataOut), .WriteReg(WriteReg), .RegWrite(RegWite), .Clock(CLK),
    .ReadData1(reg_file_1_readdata1), .ReadReg1(ReadReg1), .ReadData2(reg_file_1_readdata2),
    .ReadReg2(ReadReg2));
  WriteSelector writeselector_1 (
    .ExtWrite(ExtMemWrite), .IntData(reg_file_1_readdata2), .ExtData(ExtMemData), .Data(writeselector_1_data));
  b b_1 (
    .Address(MemAddress), .Offset(reg_file_1_readdata1), .DataLoad(writeselector_1_data), .Store(MemWrite),
    .DataOut(MemDataOut), .CLK(CLK));
endmodule
