// Logisim project 5.circ as structural Verilog: 2 circuits, main circuit main
module main (
);

  wire Control_alu, Control_memtoreg, Control_memwrite, Control_regdst, Control_regwrite;
  wire [1:0] Control_alu_op, INSTRUCTION_MEMORY_PC_p1, INSTRUCTION_MEMORY_PC_p3, INSTRUCTION_MEMORY_PC_p5,
       INSTRUCTION_MEMORY_PC_p7, multiplexer_1_out;
  wire [3:0] ALU_output, DATA_MEM_REG_dataout, multiplexer_2_out, multiplexer_3_out, undriven, undriven_2;

  // Q4B3_main INSTRUCTION_MEMORY_PC: pin names not known; wires that end beside it: INSTRUCTION_MEMORY_PC_p1[0], INSTRUCTION_MEMORY_PC_p1[1], INSTRUCTION_MEMORY_PC_p3[0], INSTRUCTION_MEMORY_PC_p3[1], INSTRUCTION_MEMORY_PC_p5[0], INSTRUCTION_MEMORY_PC_p5[1], INSTRUCTION_MEMORY_PC_p7[0], INSTRUCTION_MEMORY_PC_p7[1]
  Multiplexer #(.width(2), .enable("false")) multiplexer_1 (
    .in0(INSTRUCTION_MEMORY_PC_p5), .in1(INSTRUCTION_MEMORY_PC_p7), .out(multiplexer_1_out),
    .sel(Control_regdst));
  Multiplexer #(.width(4), .enable("false")) multiplexer_2 (
    .in0(ALU_output), .in1(DATA_MEM_REG_dataout), .out(multiplexer_2_out), .sel(Control_memtoreg));
  ControlTruth Control (
    .OpCode(INSTRUCTION_MEMORY_PC_p1), .RegDst(Control_regdst), .ALU(Control_alu),
    .MemtoReg(Control_memtoreg), .RegWrite(Control_regwrite), .MemWrite(Control_memwrite),
    .ALU_OP(Control_alu_op));  // open: MemRead
  ALU ALU (
    .Input1(undriven), .Input2(multiplexer_3_out), .ControlBits(Control_alu_op), .Output(ALU_output));  // open: CarryOut, Zero
  Multiplexer #(.width(4), .enable("false")) multiplexer_3 (
    .in0(undriven_2), .in1({INSTRUCTION_MEMORY_PC_p7, 2'b00}), .out(multiplexer_3_out), .sel(Control_alu));
  Diarmuid_Ryan_11363776_A4_main DATA_MEM_REG (
    .RegOut1(undriven), .RegOut2(undriven_2), .RegRead1(INSTRUCTION_MEMORY_PC_p3),
    .RegRead2(multiplexer_1_out), .RegWrite_2(Control_regwrite), .MemAdd(ALU_output),
    .MemWrite(Control_memwrite), .DataOut(DATA_MEM_REG_dataout), .WriteData(multiplexer_2_out));  // open: RegWrite, ExtDataWrite, ExtData, CLK

  // Notes on the sheet:
  //   OP
  //   RS
  //   RT
  //   RD/Offset
endmodule

module main2 (
  input  [7:0] DataIn
);

  wire Control_alu, Control_memtoreg, Control_memwrite, Control_regdst, Control_regwrite, main_1_p1,
       not_1_out;
  wire [1:0] Control_alu_op, main_1_p4, main_1_p6, main_1_p8, main_1_p10, multiplexer_1_out,
       multiplexer_2_out;
  wire [3:0] ALU_output, b_1_dataout, multiplexer_3_out, multiplexer_4_out, RegFile_readdata1,
       RegFile_readdata2;

  // Q4B3_main main_1: pin names not known; wires that end beside it: main_1_p1, DataIn, 1'b1, main_1_p4[0], main_1_p4[1], main_1_p6[0], main_1_p6[1], main_1_p8[0], main_1_p8[1], main_1_p10[0], main_1_p10[1]
  Multiplexer #(.width(2), .enable("false")) multiplexer_1 (
    .in0(main_1_p8), .in1(main_1_p10), .out(multiplexer_1_out), .sel(Control_regdst));
  Multiplexer #(.width(2), .enable("false")) multiplexer_2 (
    .in0(main_1_p8), .in1(main_1_p10), .out(multiplexer_2_out), .sel(not_1_out));
  not not_1 (not_1_out, Control_regdst);
  Clock clock_1 (.out(main_1_p1));
  Multiplexer #(.width(4), .enable("false")) multiplexer_3 (
    .in0(ALU_output), .in1(b_1_dataout), .out(multiplexer_3_out), .sel(Control_memtoreg));
  reg_file RegFile (
    .WriteData(multiplexer_3_out), .WriteReg(multiplexer_1_out), .RegWrite(Control_regwrite),
    .Clock(main_1_p1), .ReadData1(RegFile_readdata1), .ReadReg1(main_1_p6), .ReadData2(RegFile_readdata2),
    .ReadReg2(multiplexer_2_out));
  ControlTruth Control (
    .OpCode(main_1_p4), .RegDst(Control_regdst), .ALU(Control_alu), .MemtoReg(Control_memtoreg),
    .RegWrite(Control_regwrite), .MemWrite(Control_memwrite), .ALU_OP(Control_alu_op));  // open: MemRead
  DotMatrix #(.matrixcols(4), .matrixrows(1)) dotmatrix_1 (
    .col0(ALU_output[0]), .col1(ALU_output[1]), .col2(ALU_output[2]), .col3(ALU_output[3]));
  DotMatrix #(.matrixcols(4), .matrixrows(1)) dotmatrix_2 (
    .col0(RegFile_readdata1[0]), .col1(RegFile_readdata1[1]), .col2(RegFile_readdata1[2]),
    .col3(RegFile_readdata1[3]));
  Multiplexer #(.width(4), .enable("false")) multiplexer_4 (
    .in0(RegFile_readdata2), .in1({main_1_p10, 2'b00}), .out(multiplexer_4_out), .sel(Control_alu));
  ALU ALU (
    .Input1(RegFile_readdata1), .Input2(multiplexer_4_out), .ControlBits(Control_alu_op), .Output(ALU_output));  // open: CarryOut, Zero
  b b_1 (
    .Address(ALU_output), .DataLoad(RegFile_readdata2), .Store(Control_memwrite), .DataOut(b_1_dataout),
    .CLK(main_1_p1));  // open: Offset

  // Notes on the sheet:
  //   OP
  //   RS
  //   RT
  //   RD/Offset
endmodule
